# Fritzing sketch flora2 (saved by Fritzing 0.9.4)
perfboards: 1

parts:
  R2 = Resistor [tolerance=±5% resistance=470 package=THT]
  R3 = Resistor [tolerance=±5% resistance=470 package=THT]
  R4 = Resistor [tolerance=±5% resistance=330 package=THT]
  R5 = Resistor [tolerance=±5% resistance=330 package=THT]
  R6 = Resistor [tolerance=±5% resistance=560 package=THT]
  R7 = Resistor [tolerance=±5% resistance=560 package=THT]
  J5 = Terminal Block - 3 pins [part_number=Pump package=THT]
  R8 = Resistor [tolerance=±5% resistance=10k package=THT]
  U2 = ESP32S-HiLetgo [part_number="ESP32 DevKitC V4"]
  J3 = Terminal Block - 3 pins [part_number="Moisture Sensors A" package=THT]
  J4 = Terminal Block - 3 pins [part_number="Moisture Sensors B" package=THT]
  R10 = Resistor [tolerance=±5% resistance=220k package=THT]
  R11 = Resistor [tolerance=±5% resistance=330k package=THT]
  R12 = Resistor [tolerance=±5% resistance=220k package=THT]
  R14 = Resistor [tolerance=±5% resistance=220k package=THT]
  R15 = Resistor [tolerance=±5% resistance=330k package=THT]
  R16 = Resistor [tolerance=±5% resistance=220k package=THT]
  R17 = Resistor [tolerance=±5% resistance=330k package=THT]
  R18 = Resistor [tolerance=±5% resistance=100 package=THT]
  Q2 = Basic FET N-Channel [part_number=BTS117 package="TO220 [THT]"]
  Q4 = MOSFET-NCHANNEL [part_number=ZVP2106A package=to-92]
  J2 = Terminal Block - 3 pins [part_number="Tank Sensors" package=THT]
  J1 = Terminal Block - 3 pins [part_number=Power package=THT]
  Q3 = MOSFET-NCHANNEL [part_number=ZVN4206A package=to-92]
  Q1 = Basic FET N-Channel [part_number=BTS117 package="TO220 [THT]"]
  J6 = female pin header, 6 pins [form="♀ (female)"]
  D2 = Zener Diode [part_number=SMLVT3V3 breakdown_voltage=3.6V package="Melf DO-213 AB [SMD]"]
  D1 = Zener Diode [part_number=SMLVT3V3 breakdown_voltage=3.6V package="Melf DO-213 AB [SMD]"]
  D3 = Zener Diode [part_number=SMLVT3V3 breakdown_voltage=3.6V package="Melf DO-213 AB [SMD]"]
  D4 = Zener Diode [part_number=SMLVT3V3 breakdown_voltage=3.6V package="Melf DO-213 AB [SMD]"]
  R13 = Resistor [tolerance=±5% resistance=330k package=THT]
  J7 = male pin header, 6 pins [form="♂ (male)" part_number=GPIO1]

nets:
  5V: R2.Pin_0, R3.Pin_0, R8.Pin_1, U2.VIN, J3.Line_1, Q4.S, J1.Line_3
  N1: R2.Pin_1, R4.Pin_0, J2.Line_1
  N2: R3.Pin_1, R5.Pin_0, J2.Line_2
  ESP32_tank_low: R4.Pin_1, R6.Pin_0, U2.GPIO23
  ESP32_tank_empty: R5.Pin_1, R7.Pin_0, U2.GPIO21
  GND: R6.Pin_1, R7.Pin_1, J5.Line_3, U2.GND, J4.Line_3, R11.Pin_1, R15.Pin_1, R17.Pin_1, Q2.source, J2.Line_3, J1.Line_2, Q3.S, Q1.source, J6.pin5, D2.anode, D1.anode, D3.anode, D4.anode, R13.Pin_1, J7.pin1
  N3: J5.Line_1, Q1.drain
  N4: J5.Line_2, Q2.drain
  N5: R8.Pin_0, Q4.G, Q3.D
  3V3: U2.3.3, J6.pin1, J6.pin2, J6.pin6, J7.pin6
  ESP32_moisture1: U2.GPIO34, R10.Pin_1, R11.Pin_0, D1.cathode
  ESP32_moisture2: U2.GPIO35, R12.Pin_1, D2.cathode, R13.Pin_0
  ESP32_moisture3: U2.GPIO32, R14.Pin_1, R15.Pin_0, D3.cathode
  ESP32_moisture4: U2.GPIO33, R16.Pin_1, R17.Pin_0, D4.cathode
  I2C1_SCL: U2.GPIO25, J6.pin4
  I2C1_SDA: U2.GPIO26, J6.pin3
  N6: U2.GPIO27, J7.pin4
  N7: U2.GPIO14, J7.pin3
  N8: U2.GPIO12, J7.pin2
  ESP32_sensor_en: U2.GPIO13, R18.Pin_0
  ESP32_pump2_ctrl: U2.GPIO18, Q2.gate
  ESP32_pump1_ctrl: U2.GPIO19, Q1.gate
  N9: J3.Line_2, R10.Pin_0
  N10: J3.Line_3, R12.Pin_0
  N11: J4.Line_1, R14.Pin_0
  N12: J4.Line_2, R16.Pin_0
  N13: R18.Pin_1, Q3.G
  Sensor_PWR: Q4.D, J1.Line_1

notes:
  GND
  VCC
  SCK/SCL
  SDI/SDA
  CSB
  SDO/ADDR
  Sensor_PWR
  5V
  Tank_low
  Tank_empty
  Pump1_GND
  Pump2_GND
  Flora2, ESP32 Irrigation Controller, 0.2
  Moisture1
  Moisture2
  Moisture3
  Moisture4

custom parts:
  Terminal Block - 3 pins: Generic Screw Terminal 9.5mm
  ESP32S-HiLetgo: HiLetgo ESP-WROOM-32 ESP32 ESP-32S Development Board 2.4GHz Dual-Mode WiFi + Bluetooth Dual Cores Microcontroller The ESP32 integrated with Antenna switches, RF Balun, power amplifiers, low-noise amplifiers, filters, and management modules, and the entire solution occupies the least area of PCB. 2.4 GHz Wi-Fi plus Bluetooth dual-mode chip, with TSMC Ultra-low power consumption 40nm technology,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
  MOSFET-NCHANNEL: Generic NMOS footprint
  MOSFET-NCHANNEL: Generic NMOS footprint
